// Logisim project ‌Basic Computer.circ as structural Verilog: 30 circuits, main circuit main
module main (
  input  [7:0] in_1,
  output [7:0] out_2
);

  wire ac_controller_1_clr, ac_controller_1_inr, ar_controller_1_clr, ar_controller_1_inr,
       ar_controller_1_ld, CLK, clock_1_out, Cout, dr_controller_1_inr, dr_controller_1_ld, E,
       e_controller_1_j, e_controller_1_k, FGI, fgi_controller_1_j, fgi_controller_1_k, FGO,
       fgo_controller_1_j, fgo_controller_1_k, hlt_1_out_4, I, i_controller_1_j, i_controller_1_k, IEN,
       ien_controller_1_j, ien_controller_1_k, ir_controller_1_ld, memory_controller_1_read,
       memory_controller_1_write, not_1_out, or_1_out, outr_controller_1_ld, pc_controller_1_clr,
       pc_controller_1_inr, pc_controller_1_ld, R, r_controller_1_j, r_controller_1_k, S, s2_s1_s0_1_s0,
       s2_s1_s0_1_s1, s2_s1_s0_1_s2, s_controller_1_k, sc_controller_1_clr, sc_controller_1_inr,
       tr_controller_1_ld;
  wire [3:0] sc_1_output;
  wire [6:0] ac_controller_1_ld;
  wire [7:0] _8, INPR;
  wire [11:0] _12, n12_bit_reg_1_output, n12_bit_reg_2_output;
  wire [15:0] _16, AC, alu_1_out_7, DR, IR, ram_1_data, T, TR;

  Clock clock_1 (.out(clock_1_out));
  HLT hlt_1 (.I(I), .T(T), .IR(IR), .out_4(hlt_1_out_4));
  I_controller i_controller_1 (.IR(IR), .T(T), .R(R), .J(i_controller_1_j), .K(i_controller_1_k));
  R_controller r_controller_1 (
    .in_1(R), .in_2(IEN), .T(T), .in_4(FGI), .in_5(FGO), .J(r_controller_1_j), .K(r_controller_1_k));
  FGI_controller fgi_controller_1 (.I(I), .T(T), .IR(IR), .INPR(INPR), .J(fgi_controller_1_j), .K(fgi_controller_1_k));
  FGO_controller fgo_controller_1 (.I(I), .T(T), .IR(IR), .J(fgo_controller_1_j), .K(fgo_controller_1_k));
  IEN_controller ien_controller_1 (.I(I), .T(T), .IR(IR), .R(R), .J(ien_controller_1_j), .K(ien_controller_1_k));
  SC_controller sc_controller_1 (
    .I(I), .T(T), .IR(IR), .R(R), .in_5(S), .CLR(sc_controller_1_clr), .INR(sc_controller_1_inr));
  not not_1 (not_1_out, hlt_1_out_4);
  E_controller e_controller_1 (
    .I(I), .T(T), .IR(IR), .in_4(AC), .in_5(Cout), .J(e_controller_1_j), .K(e_controller_1_k));
  S_controller s_controller_1 (.I(I), .T(T), .IR(IR), .K(s_controller_1_k));
  SC sc_1 (.INR(sc_controller_1_inr), .CLK(CLK), .\output (sc_1_output), .CLR(sc_controller_1_clr));
  and and_1 (CLK, clock_1_out, not_1_out);
  J_K_Flip_Flop u_I (.J(i_controller_1_j), .clk(CLK), .K(i_controller_1_k), .Q(I));  // open: Qn, preset, en, reset
  J_K_Flip_Flop u_R (.J(r_controller_1_j), .clk(CLK), .K(r_controller_1_k), .Q(R));  // open: Qn, preset, en, reset
  J_K_Flip_Flop u_E (.J(e_controller_1_j), .clk(CLK), .K(e_controller_1_k), .Q(E));  // open: Qn, preset, en, reset
  J_K_Flip_Flop u_S (.clk(CLK), .K(s_controller_1_k), .Q(S));  // open: J, Qn, preset, en, reset
  J_K_Flip_Flop u_FGI (
    .J(fgi_controller_1_j), .clk(CLK), .K(fgi_controller_1_k), .Q(FGI));  // open: Qn, preset, en, reset
  J_K_Flip_Flop u_FGO (
    .J(fgo_controller_1_j), .clk(CLK), .K(fgo_controller_1_k), .Q(FGO));  // open: Qn, preset, en, reset
  J_K_Flip_Flop u_IEN (
    .J(ien_controller_1_j), .clk(CLK), .K(ien_controller_1_k), .Q(IEN));  // open: Qn, preset, en, reset
  Decoder #(.select(4)) decoder_1 (
    .out0(T[0]), .out1(T[1]), .out2(T[2]), .out3(T[3]), .out4(T[4]), .out5(T[5]), .out6(T[6]), .out7(T[7]),
    .out8(T[8]), .out9(T[9]), .out10(T[10]), .out11(T[11]), .out12(T[12]), .out13(T[13]), .out14(T[14]),
    .out15(T[15]), .sel(sc_1_output));  // open: en
  // Probe on T
  // Probe on ac_controller_1_ld
  // Probe on _16
  ALU alu_1 (.in_1(AC), .DR(DR), .in_3(INPR), .out_7(alu_1_out_7), .in_4(ac_controller_1_ld), .in_5(E), .C_out(Cout));
  // Probe on _16
  // Probe on alu_1_out_7
  // Probe on Cout
  Memory_controller memory_controller_1 (
    .I(I), .T(T), .IR(IR), .R(R), .READ(memory_controller_1_read), .WRITE(memory_controller_1_write));
  AR_controller ar_controller_1 (
    .I(I), .T(T), .IR(IR), .R(R), .LD(ar_controller_1_ld), .INR(ar_controller_1_inr),
    .CLR(ar_controller_1_clr));
  DR_controller dr_controller_1 (.T(T), .IR(IR), .LD(dr_controller_1_ld), .INR(dr_controller_1_inr));
  or or_1 (or_1_out, ac_controller_1_ld[6], ac_controller_1_ld[5], ac_controller_1_ld[4], ac_controller_1_ld[3], ac_controller_1_ld[2], ac_controller_1_ld[1], ac_controller_1_ld[0]);
  AC_controller ac_controller_1 (
    .I(I), .T(T), .IR(IR), .R(R), .LD(ac_controller_1_ld), .INR(ac_controller_1_inr),
    .CLR(ac_controller_1_clr));
  INPR inpr_1 (.IN(in_1), .CLK(CLK), .OUT(INPR));
  IR_controller ir_controller_1 (.T(T), .in_2(R), .LD(ir_controller_1_ld));
  TR_controller tr_controller_1 (.T(T), .in_2(R), .LD(tr_controller_1_ld));
  PC_controller pc_controller_1 (
    .in_1(I), .in_2(R), .in_3(E), .in_4(FGI), .T(T), .in_6(FGO), .IR(IR), .DR(DR), .in_9(AC),
    .INR(pc_controller_1_inr), .LD(pc_controller_1_ld), .CLR(pc_controller_1_clr));
  OUTR outr_1 (.IN(_8), .LD(outr_controller_1_ld), .CLK(CLK), .OUT(out_2));
  OUTR_controller outr_controller_1 (.I(I), .T(T), .IR(IR), .LD(outr_controller_1_ld));
  RAM #(.addrWidth(12), .dataWidth(16), .bus("separate")) ram_1 (
    .addr(n12_bit_reg_1_output), .din(_16), .data(ram_1_data), .str(memory_controller_1_write), .clk(CLK),
    .ld(memory_controller_1_read));  // open: sel, clr
  _12_bit_reg u_12_bit_reg_1 (
    .in_1(_12), .INR(ar_controller_1_inr), .LD(ar_controller_1_ld), .in_4(CLK), .in_5(ar_controller_1_clr),
    .\output (n12_bit_reg_1_output));
  _12_bit_reg u_12_bit_reg_2 (
    .in_1(_12), .INR(pc_controller_1_inr), .LD(pc_controller_1_ld), .in_4(CLK), .in_5(pc_controller_1_clr),
    .\output (n12_bit_reg_2_output));
  _16bit_reg u_16bit_reg_1 (
    .LD(dr_controller_1_ld), .in_4(CLK), .\output (DR), .INR(dr_controller_1_inr), .in_5(1'b0), .in_1(_16));
  _16bit_reg u_16bit_reg_2 (
    .LD(or_1_out), .in_4(CLK), .\output (AC), .INR(ac_controller_1_inr), .in_5(ac_controller_1_clr),
    .in_1(alu_1_out_7));
  _16bit_reg u_16bit_reg_3 (.LD(ir_controller_1_ld), .in_4(CLK), .\output (IR), .INR(1'b0), .in_5(1'b0), .in_1(_16));
  _16bit_reg u_16bit_reg_4 (.LD(tr_controller_1_ld), .in_4(CLK), .\output (TR), .INR(1'b0), .in_5(1'b0), .in_1(_16));
  // Probe on ram_1_data
  // Probe on n12_bit_reg_1_output
  // Probe on n12_bit_reg_2_output
  // Probe on DR
  // Probe on AC
  // Probe on IR
  // Probe on TR
  S2_S1_S0 s2_s1_s0_1 (.I(I), .T(T), .IR(IR), .R(R), .S2(s2_s1_s0_1_s2), .S1(s2_s1_s0_1_s1), .S0(s2_s1_s0_1_s0));
  BUS bus_1 (
    .S2(s2_s1_s0_1_s2), .in_2(n12_bit_reg_1_output), .in_3(n12_bit_reg_2_output), .in_4(DR),
    .S1(s2_s1_s0_1_s1), .in_6(AC), .in_7(IR), .S0(s2_s1_s0_1_s0), .in_9(TR), .in_10(ram_1_data),
    ._16bit(_16), ._12bit(_12), ._8bit(_8));

  // Notes on the sheet:
  //   AR
  //   PC
  //   DR
  //   AC
  //   IR
  //   TR
endmodule

module adder__1_bit (
  input  Cin,
  input  A,
  input  B,
  output S,
  output Cout
);

  wire and_1_out, and_2_out, xor_1_out;

  xor xor_1 (xor_1_out, A, B);
  and and_1 (and_1_out, A, B);
  xor xor_2 (S, Cin, xor_1_out);
  and and_2 (and_2_out, Cin, xor_1_out);
  or or_1 (Cout, and_2_out, and_1_out);
endmodule

module increment__16_bit (
  input  [15:0] in_1,
  output [15:0] \output 
);

  wire adder_1_bit_1_cout, adder_1_bit_2_cout, adder_1_bit_3_cout, adder_1_bit_4_cout, adder_1_bit_5_cout,
       adder_1_bit_6_cout, adder_1_bit_7_cout, adder_1_bit_8_cout, adder_1_bit_9_cout, adder_1_bit_10_cout,
       adder_1_bit_11_cout, adder_1_bit_12_cout, adder_1_bit_13_cout, adder_1_bit_14_cout, C_7;

  adder__1_bit adder_1_bit_1 (.Cin(1'b0), .A(in_1[0]), .B(1'b1), .S(\output [0]), .Cout(adder_1_bit_1_cout));
  adder__1_bit adder_1_bit_2 (.Cin(C_7), .A(in_1[8]), .B(1'b0), .S(\output [8]), .Cout(adder_1_bit_2_cout));
  adder__1_bit adder_1_bit_3 (
    .Cin(adder_1_bit_1_cout), .A(in_1[1]), .B(1'b0), .S(\output [1]), .Cout(adder_1_bit_3_cout));
  adder__1_bit adder_1_bit_4 (
    .Cin(adder_1_bit_2_cout), .A(in_1[9]), .B(1'b0), .S(\output [9]), .Cout(adder_1_bit_4_cout));
  adder__1_bit adder_1_bit_5 (
    .Cin(adder_1_bit_3_cout), .A(in_1[2]), .B(1'b0), .S(\output [2]), .Cout(adder_1_bit_5_cout));
  adder__1_bit adder_1_bit_6 (
    .Cin(adder_1_bit_4_cout), .A(in_1[10]), .B(1'b0), .S(\output [10]), .Cout(adder_1_bit_6_cout));
  adder__1_bit adder_1_bit_7 (
    .Cin(adder_1_bit_5_cout), .A(in_1[3]), .B(1'b0), .S(\output [3]), .Cout(adder_1_bit_7_cout));
  adder__1_bit adder_1_bit_8 (
    .Cin(adder_1_bit_6_cout), .A(in_1[11]), .B(1'b0), .S(\output [11]), .Cout(adder_1_bit_8_cout));
  adder__1_bit adder_1_bit_9 (
    .Cin(adder_1_bit_7_cout), .A(in_1[4]), .B(1'b0), .S(\output [4]), .Cout(adder_1_bit_9_cout));
  adder__1_bit adder_1_bit_10 (
    .Cin(adder_1_bit_8_cout), .A(in_1[12]), .B(1'b0), .S(\output [12]), .Cout(adder_1_bit_10_cout));
  adder__1_bit adder_1_bit_11 (
    .Cin(adder_1_bit_9_cout), .A(in_1[5]), .B(1'b0), .S(\output [5]), .Cout(adder_1_bit_11_cout));
  adder__1_bit adder_1_bit_12 (
    .Cin(adder_1_bit_10_cout), .A(in_1[13]), .B(1'b0), .S(\output [13]), .Cout(adder_1_bit_12_cout));
  adder__1_bit adder_1_bit_13 (
    .Cin(adder_1_bit_11_cout), .A(in_1[6]), .B(1'b0), .S(\output [6]), .Cout(adder_1_bit_13_cout));
  adder__1_bit adder_1_bit_14 (
    .Cin(adder_1_bit_12_cout), .A(in_1[14]), .B(1'b0), .S(\output [14]), .Cout(adder_1_bit_14_cout));
  adder__1_bit adder_1_bit_15 (.Cin(adder_1_bit_13_cout), .A(in_1[7]), .B(1'b0), .S(\output [7]), .Cout(C_7));
  adder__1_bit adder_1_bit_16 (.Cin(adder_1_bit_14_cout), .A(in_1[15]), .B(1'b0), .S(\output [15]));  // open: Cout

  // Other names for the same wires on the sheet: A_0 = in_1[0]; A_1 = in_1[1]; A_2 = in_1[2]; A_3 = in_1[3];
  //   A_4 = in_1[4]; A_5 = in_1[5]; A_6 = in_1[6]; A_7 = in_1[7]; A_8 = in_1[8]; A_9 = in_1[9]; A_10 = in_1[10];
  //   A_11 = in_1[11]; A_12 = in_1[12]; A_13 = in_1[13]; A_14 = in_1[14]; A_15 = in_1[15]; B_0 = \output [0];
  //   B_1 = \output [1]; B_2 = \output [2]; B_3 = \output [3]; B_4 = \output [4]; B_5 = \output [5];
  //   B_6 = \output [6]; B_7 = \output [7]; B_8 = \output [8]; B_9 = \output [9]; B_10 = \output [10];
  //   B_11 = \output [11]; B_12 = \output [12]; B_13 = \output [13]; B_14 = \output [14]; B_15 = \output [15]
endmodule

module increment__12_bit (
  input  [11:0] in_1,
  output [11:0] \output 
);

  wire adder_1_bit_1_cout, adder_1_bit_2_cout, adder_1_bit_3_cout, adder_1_bit_4_cout, adder_1_bit_5_cout,
       adder_1_bit_6_cout, adder_1_bit_7_cout, adder_1_bit_9_cout, adder_1_bit_10_cout, adder_1_bit_11_cout,
       C_7;

  adder__1_bit adder_1_bit_1 (.Cin(1'b0), .A(in_1[0]), .B(1'b1), .S(\output [0]), .Cout(adder_1_bit_1_cout));
  adder__1_bit adder_1_bit_2 (.Cin(C_7), .A(in_1[8]), .B(1'b0), .S(\output [8]), .Cout(adder_1_bit_2_cout));
  adder__1_bit adder_1_bit_3 (
    .Cin(adder_1_bit_1_cout), .A(in_1[1]), .B(1'b0), .S(\output [1]), .Cout(adder_1_bit_3_cout));
  adder__1_bit adder_1_bit_4 (
    .Cin(adder_1_bit_2_cout), .A(in_1[9]), .B(1'b0), .S(\output [9]), .Cout(adder_1_bit_4_cout));
  adder__1_bit adder_1_bit_5 (
    .Cin(adder_1_bit_3_cout), .A(in_1[2]), .B(1'b0), .S(\output [2]), .Cout(adder_1_bit_5_cout));
  adder__1_bit adder_1_bit_6 (
    .Cin(adder_1_bit_4_cout), .A(in_1[10]), .B(1'b0), .S(\output [10]), .Cout(adder_1_bit_6_cout));
  adder__1_bit adder_1_bit_7 (
    .Cin(adder_1_bit_5_cout), .A(in_1[3]), .B(1'b0), .S(\output [3]), .Cout(adder_1_bit_7_cout));
  adder__1_bit adder_1_bit_8 (.Cin(adder_1_bit_6_cout), .A(in_1[11]), .B(1'b0), .S(\output [11]));  // open: Cout
  adder__1_bit adder_1_bit_9 (
    .Cin(adder_1_bit_7_cout), .A(in_1[4]), .B(1'b0), .S(\output [4]), .Cout(adder_1_bit_9_cout));
  adder__1_bit adder_1_bit_10 (
    .Cin(adder_1_bit_9_cout), .A(in_1[5]), .B(1'b0), .S(\output [5]), .Cout(adder_1_bit_10_cout));
  adder__1_bit adder_1_bit_11 (
    .Cin(adder_1_bit_10_cout), .A(in_1[6]), .B(1'b0), .S(\output [6]), .Cout(adder_1_bit_11_cout));
  adder__1_bit adder_1_bit_12 (.Cin(adder_1_bit_11_cout), .A(in_1[7]), .B(1'b0), .S(\output [7]), .Cout(C_7));

  // Other names for the same wires on the sheet: A_0 = in_1[0]; A_1 = in_1[1]; A_2 = in_1[2]; A_3 = in_1[3];
  //   A_4 = in_1[4]; A_5 = in_1[5]; A_6 = in_1[6]; A_7 = in_1[7]; A_8 = in_1[8]; A_9 = in_1[9]; A_10 = in_1[10];
  //   A_11 = in_1[11]; B_0 = \output [0]; B_1 = \output [1]; B_2 = \output [2]; B_3 = \output [3]; B_4 = \output [4];
  //   B_5 = \output [5]; B_6 = \output [6]; B_7 = \output [7]; B_8 = \output [8]; B_9 = \output [9];
  //   B_10 = \output [10]; B_11 = \output [11]
endmodule

module ALU__1_bit (
  input  in_1,
  input  in_2,
  input  C_i,
  input  [6:0] in_4,
  input  INPR_i,
  input  AC_i_1,
  input  AC_i_1_2,
  output C_i_1,
  output AC_i
);

  wire adder_1_bit_1_s, and_1_out, and_2_out, and_3_out, and_4_out, and_5_out, and_6_out, and_7_out,
       not_1_out, or_1_out, or_2_out;

  adder__1_bit adder_1_bit_1 (.Cin(C_i), .A(in_1), .B(in_2), .S(adder_1_bit_1_s), .Cout(C_i_1));
  not not_1 (not_1_out, in_1);
  and and_1 (and_1_out, in_4[0], in_1, in_2);
  and and_2 (and_2_out, in_4[1], adder_1_bit_1_s);
  and and_3 (and_3_out, in_4[2], in_2);
  and and_4 (and_4_out, in_4[3], INPR_i);
  and and_5 (and_5_out, in_4[4], not_1_out);
  and and_6 (and_6_out, in_4[5], AC_i_1);
  and and_7 (and_7_out, in_4[6], AC_i_1_2);
  or or_1 (or_1_out, and_1_out, and_2_out, and_3_out, and_4_out, and_5_out, and_6_out, and_7_out);
  or or_2 (or_2_out, in_4[6], in_4[5], in_4[4], in_4[3], in_4[2], in_4[1], in_4[0]);
  and and_8 (AC_i, or_1_out, or_2_out);

  // Other names for the same wires on the sheet: AC_i_t = in_1; AND = in_4[0]; CTRL[6:0] = in_4; ADD = in_4[1];
  //   DR = in_4[2]; INPR = in_4[3]; COM = in_4[4]; SHR = in_4[5]; SHL = in_4[6]; DR_i = in_2
endmodule

module ALU (
  input  [15:0] in_1,
  input  [15:0] DR,
  input  [7:0] in_3,
  input  [6:0] in_4,
  input  in_5,
  output C_out,
  output [15:0] out_7
);

  wire alu_1_bit_1_c_i_1, alu_1_bit_2_c_i_1, alu_1_bit_3_c_i_1, alu_1_bit_5_c_i_1, alu_1_bit_6_c_i_1,
       alu_1_bit_7_c_i_1, alu_1_bit_9_c_i_1, alu_1_bit_10_c_i_1, alu_1_bit_11_c_i_1, alu_1_bit_13_c_i_1,
       alu_1_bit_14_c_i_1, alu_1_bit_15_c_i_1, C_3, C_7, C_11;

  ALU__1_bit alu_1_bit_1 (
    .in_1(in_1[0]), .in_2(DR[0]), .C_i(1'b0), .in_4(in_4), .INPR_i(in_3[0]), .AC_i_1(in_1[1]),
    .AC_i_1_2(in_5), .C_i_1(alu_1_bit_1_c_i_1), .AC_i(out_7[0]));
  ALU__1_bit alu_1_bit_2 (
    .in_1(in_1[1]), .in_2(DR[1]), .C_i(alu_1_bit_1_c_i_1), .in_4(in_4), .INPR_i(in_3[1]), .AC_i_1(in_1[2]),
    .AC_i_1_2(in_1[0]), .C_i_1(alu_1_bit_2_c_i_1), .AC_i(out_7[1]));
  ALU__1_bit alu_1_bit_3 (
    .in_1(in_1[2]), .in_2(DR[2]), .C_i(alu_1_bit_2_c_i_1), .in_4(in_4), .INPR_i(in_3[2]), .AC_i_1(in_1[3]),
    .AC_i_1_2(in_1[1]), .C_i_1(alu_1_bit_3_c_i_1), .AC_i(out_7[2]));
  ALU__1_bit alu_1_bit_4 (
    .in_1(in_1[3]), .in_2(DR[3]), .C_i(alu_1_bit_3_c_i_1), .in_4(in_4), .INPR_i(in_3[3]), .AC_i_1(in_1[4]),
    .AC_i_1_2(in_1[2]), .C_i_1(C_3), .AC_i(out_7[3]));
  ALU__1_bit alu_1_bit_5 (
    .in_1(in_1[4]), .in_2(DR[4]), .C_i(C_3), .in_4(in_4), .INPR_i(in_3[4]), .AC_i_1(in_1[5]),
    .AC_i_1_2(in_1[3]), .C_i_1(alu_1_bit_5_c_i_1), .AC_i(out_7[4]));
  ALU__1_bit alu_1_bit_6 (
    .in_1(in_1[5]), .in_2(DR[5]), .C_i(alu_1_bit_5_c_i_1), .in_4(in_4), .INPR_i(in_3[5]), .AC_i_1(in_1[6]),
    .AC_i_1_2(in_1[4]), .C_i_1(alu_1_bit_6_c_i_1), .AC_i(out_7[5]));
  ALU__1_bit alu_1_bit_7 (
    .in_1(in_1[6]), .in_2(DR[6]), .C_i(alu_1_bit_6_c_i_1), .in_4(in_4), .INPR_i(in_3[6]), .AC_i_1(in_1[7]),
    .AC_i_1_2(in_1[5]), .C_i_1(alu_1_bit_7_c_i_1), .AC_i(out_7[6]));
  ALU__1_bit alu_1_bit_8 (
    .in_1(in_1[7]), .in_2(DR[7]), .C_i(alu_1_bit_7_c_i_1), .in_4(in_4), .INPR_i(in_3[7]), .AC_i_1(in_1[8]),
    .AC_i_1_2(in_1[6]), .C_i_1(C_7), .AC_i(out_7[7]));
  ALU__1_bit alu_1_bit_9 (
    .in_1(in_1[8]), .in_2(DR[8]), .C_i(C_7), .in_4(in_4), .INPR_i(1'b0), .AC_i_1(in_1[9]),
    .AC_i_1_2(in_1[7]), .C_i_1(alu_1_bit_9_c_i_1), .AC_i(out_7[8]));
  ALU__1_bit alu_1_bit_10 (
    .in_1(in_1[9]), .in_2(DR[9]), .C_i(alu_1_bit_9_c_i_1), .in_4(in_4), .INPR_i(1'b0), .AC_i_1(in_1[10]),
    .AC_i_1_2(in_1[8]), .C_i_1(alu_1_bit_10_c_i_1), .AC_i(out_7[9]));
  ALU__1_bit alu_1_bit_11 (
    .in_1(in_1[10]), .in_2(DR[10]), .C_i(alu_1_bit_10_c_i_1), .in_4(in_4), .INPR_i(1'b0), .AC_i_1(in_1[11]),
    .AC_i_1_2(in_1[9]), .C_i_1(alu_1_bit_11_c_i_1), .AC_i(out_7[10]));
  ALU__1_bit alu_1_bit_12 (
    .in_1(in_1[11]), .in_2(DR[11]), .C_i(alu_1_bit_11_c_i_1), .in_4(in_4), .INPR_i(1'b0), .AC_i_1(in_1[12]),
    .AC_i_1_2(in_1[10]), .C_i_1(C_11), .AC_i(out_7[11]));
  ALU__1_bit alu_1_bit_13 (
    .in_1(in_1[12]), .in_2(DR[12]), .C_i(C_11), .in_4(in_4), .INPR_i(1'b0), .AC_i_1(in_1[13]),
    .AC_i_1_2(in_1[11]), .C_i_1(alu_1_bit_13_c_i_1), .AC_i(out_7[12]));
  ALU__1_bit alu_1_bit_14 (
    .in_1(in_1[13]), .in_2(DR[13]), .C_i(alu_1_bit_13_c_i_1), .in_4(in_4), .INPR_i(1'b0), .AC_i_1(in_1[14]),
    .AC_i_1_2(in_1[12]), .C_i_1(alu_1_bit_14_c_i_1), .AC_i(out_7[13]));
  ALU__1_bit alu_1_bit_15 (
    .in_1(in_1[14]), .in_2(DR[14]), .C_i(alu_1_bit_14_c_i_1), .in_4(in_4), .INPR_i(1'b0), .AC_i_1(in_1[15]),
    .AC_i_1_2(in_1[13]), .C_i_1(alu_1_bit_15_c_i_1), .AC_i(out_7[14]));
  ALU__1_bit alu_1_bit_16 (
    .in_1(in_1[15]), .in_2(DR[15]), .C_i(alu_1_bit_15_c_i_1), .in_4(in_4), .INPR_i(1'b0), .AC_i_1(in_5),
    .AC_i_1_2(in_1[14]), .C_i_1(C_out), .AC_i(out_7[15]));

  // Other names for the same wires on the sheet: CTRL[6:0] = in_4; DR_0 = DR[0]; DR_1 = DR[1]; DR_2 = DR[2];
  //   DR_3 = DR[3]; DR_4 = DR[4]; DR_5 = DR[5]; DR_6 = DR[6]; DR_7 = DR[7]; DR_8 = DR[8]; DR_9 = DR[9];
  //   DR_10 = DR[10]; DR_11 = DR[11]; DR_12 = DR[12]; DR_13 = DR[13]; DR_14 = DR[14]; DR_15 = DR[15]; E = in_5;
  //   AC_0 = in_1[0]; AC_1 = in_1[1]; AC_2 = in_1[2]; AC_3 = in_1[3]; AC_4 = in_1[4]; AC_5 = in_1[5]; AC_6 = in_1[6];
  //   AC_7 = in_1[7]; AC_8 = in_1[8]; AC_9 = in_1[9]; AC_10 = in_1[10]; AC_11 = in_1[11]; AC_12 = in_1[12];
  //   AC_13 = in_1[13]; AC_14 = in_1[14]; AC_15 = in_1[15]; INPR_0 = in_3[0]; INPR_1 = in_3[1]; INPR_2 = in_3[2];
  //   INPR_3 = in_3[3]; INPR_4 = in_3[4]; INPR_5 = in_3[5]; INPR_6 = in_3[6]; INPR_7 = in_3[7]; OUT_0 = out_7[0];
  //   OUT_1 = out_7[1]; OUT_2 = out_7[2]; OUT_3 = out_7[3]; OUT_4 = out_7[4]; OUT_5 = out_7[5]; OUT_6 = out_7[6];
  //   OUT_7_t = out_7[7]; OUT_8 = out_7[8]; OUT_9 = out_7[9]; OUT_10 = out_7[10]; OUT_11 = out_7[11];
  //   OUT_12 = out_7[12]; OUT_13 = out_7[13]; OUT_14 = out_7[14]; OUT_15 = out_7[15]

  // Notes on the sheet:
  //   AC
  //   INPR
endmodule

module _16bit_reg (
  input  [15:0] in_1,
  input  INR,
  input  LD,
  input  in_4,
  input  in_5,
  output [15:0] \output 
);

  wire or_1_out;
  wire [15:0] increment_16_bit_1_output, multiplexer_1_out;

  or or_1 (or_1_out, INR, LD);
  Multiplexer #(.width(16)) multiplexer_1 (
    .in0(in_1), .in1(increment_16_bit_1_output), .out(multiplexer_1_out), .sel(INR));  // open: en
  Shift_Register #(.length(16)) shift_register_1 (
    .shift(1'b0), .clk(in_4), .load(or_1_out), .clr(in_5), .d0(multiplexer_1_out[15]), .q0(\output [15]),
    .d1(multiplexer_1_out[14]), .q1(\output [14]), .d2(multiplexer_1_out[13]), .q2(\output [13]),
    .d3(multiplexer_1_out[12]), .q3(\output [12]), .d4(multiplexer_1_out[11]), .q4(\output [11]),
    .d5(multiplexer_1_out[10]), .q5(\output [10]), .d6(multiplexer_1_out[9]), .q6(\output [9]),
    .d7(multiplexer_1_out[8]), .q7(\output [8]), .d8(multiplexer_1_out[7]), .q8(\output [7]),
    .d9(multiplexer_1_out[6]), .q9(\output [6]), .d10(multiplexer_1_out[5]), .q10(\output [5]),
    .d11(multiplexer_1_out[4]), .q11(\output [4]), .d12(multiplexer_1_out[3]), .q12(\output [3]),
    .d13(multiplexer_1_out[2]), .q13(\output [2]), .d14(multiplexer_1_out[1]), .q14(\output [1]),
    .d15(multiplexer_1_out[0]), .q15(\output [0]));  // open: in, out
  increment__16_bit increment_16_bit_1 (.in_1(\output ), .\output (increment_16_bit_1_output));

  // Notes on the sheet:
  //   CLK
  //   CLR
endmodule

module _12_bit_reg (
  input  [11:0] in_1,
  input  INR,
  input  LD,
  input  in_4,
  input  in_5,
  output [11:0] \output 
);

  wire or_1_out;
  wire [11:0] increment_12_bit_1_output, multiplexer_1_out;

  or or_1 (or_1_out, INR, LD);
  Multiplexer #(.width(12)) multiplexer_1 (
    .in0(in_1), .in1(increment_12_bit_1_output), .out(multiplexer_1_out), .sel(INR));  // open: en
  Shift_Register #(.length(12)) shift_register_1 (
    .shift(1'b0), .clk(in_4), .load(or_1_out), .clr(in_5), .d0(multiplexer_1_out[11]), .q0(\output [11]),
    .d1(multiplexer_1_out[10]), .q1(\output [10]), .d2(multiplexer_1_out[9]), .q2(\output [9]),
    .d3(multiplexer_1_out[8]), .q3(\output [8]), .d4(multiplexer_1_out[7]), .q4(\output [7]),
    .d5(multiplexer_1_out[6]), .q5(\output [6]), .d6(multiplexer_1_out[5]), .q6(\output [5]),
    .d7(multiplexer_1_out[4]), .q7(\output [4]), .d8(multiplexer_1_out[3]), .q8(\output [3]),
    .d9(multiplexer_1_out[2]), .q9(\output [2]), .d10(multiplexer_1_out[1]), .q10(\output [1]),
    .d11(multiplexer_1_out[0]), .q11(\output [0]));  // open: in, out
  increment__12_bit increment_12_bit_1 (.in_1(\output ), .\output (increment_12_bit_1_output));

  // Notes on the sheet:
  //   CLK
  //   CLR
endmodule

module BUS (
  input  S2,
  input  [11:0] in_2,
  input  [11:0] in_3,
  input  [15:0] in_4,
  input  S1,
  input  [15:0] in_6,
  input  [15:0] in_7,
  input  S0,
  input  [15:0] in_9,
  input  [15:0] in_10,
  output [15:0] _16bit,
  output [11:0] _12bit,
  output [7:0] _8bit
);

  Multiplexer #(.select(3)) multiplexer_1 (
    .in1(in_2[10]), .in2(in_3[10]), .in3(in_4[10]), .in4(in_6[10]), .in5(in_7[10]), .in6(in_9[10]),
    .in7(in_10[10]), .out(_12bit[10]), .sel({S0, S1, S2}));  // open: in0, en
  Multiplexer #(.select(3)) multiplexer_2 (
    .in1(in_2[11]), .in2(in_3[11]), .in3(in_4[11]), .in4(in_6[11]), .in5(in_7[11]), .in6(in_9[11]),
    .in7(in_10[11]), .out(_12bit[11]), .sel({S0, S1, S2}));  // open: in0, en
  Multiplexer #(.select(3)) multiplexer_3 (
    .in1(1'b0), .in2(1'b0), .in3(in_4[12]), .in4(in_6[12]), .in5(in_7[12]), .in6(in_9[12]), .in7(in_10[12]),
    .out(_16bit[12]), .sel({S0, S1, S2}));  // open: in0, en
  Multiplexer #(.select(3)) multiplexer_4 (
    .in1(in_2[0]), .in2(in_3[0]), .in3(in_4[0]), .in4(in_6[0]), .in5(in_7[0]), .in6(in_9[0]), .in7(in_10[0]),
    .out(_8bit[0]), .sel({S0, S1, S2}));  // open: in0, en
  Multiplexer #(.select(3)) multiplexer_5 (
    .in1(in_2[5]), .in2(in_3[5]), .in3(in_4[5]), .in4(in_6[5]), .in5(in_7[5]), .in6(in_9[5]), .in7(in_10[5]),
    .out(_8bit[5]), .sel({S0, S1, S2}));  // open: in0, en
  Multiplexer #(.select(3)) multiplexer_6 (
    .in1(1'b0), .in2(1'b0), .in3(in_4[13]), .in4(in_6[13]), .in5(in_7[13]), .in6(in_9[13]), .in7(in_10[13]),
    .out(_16bit[13]), .sel({S0, S1, S2}));  // open: in0, en
  Multiplexer #(.select(3)) multiplexer_7 (
    .in1(in_2[1]), .in2(in_3[1]), .in3(in_4[1]), .in4(in_6[1]), .in5(in_7[1]), .in6(in_9[1]), .in7(in_10[1]),
    .out(_8bit[1]), .sel({S0, S1, S2}));  // open: in0, en
  Multiplexer #(.select(3)) multiplexer_8 (
    .in1(in_2[6]), .in2(in_3[6]), .in3(in_4[6]), .in4(in_6[6]), .in5(in_7[6]), .in6(in_9[6]), .in7(in_10[6]),
    .out(_8bit[6]), .sel({S0, S1, S2}));  // open: in0, en
  Multiplexer #(.select(3)) multiplexer_9 (
    .in1(in_2[2]), .in2(in_3[2]), .in3(in_4[2]), .in4(in_6[2]), .in5(in_7[2]), .in6(in_9[2]), .in7(in_10[2]),
    .out(_8bit[2]), .sel({S0, S1, S2}));  // open: in0, en
  Multiplexer #(.select(3)) multiplexer_10 (
    .in1(in_2[7]), .in2(in_3[7]), .in3(in_4[7]), .in4(in_6[7]), .in5(in_7[7]), .in6(in_9[7]), .in7(in_10[7]),
    .out(_8bit[7]), .sel({S0, S1, S2}));  // open: in0, en
  Multiplexer #(.select(3)) multiplexer_11 (
    .in1(1'b0), .in2(1'b0), .in3(in_4[14]), .in4(in_6[14]), .in5(in_7[14]), .in6(in_9[14]), .in7(in_10[14]),
    .out(_16bit[14]), .sel({S0, S1, S2}));  // open: in0, en
  Multiplexer #(.select(3)) multiplexer_12 (
    .in1(in_2[3]), .in2(in_3[3]), .in3(in_4[3]), .in4(in_6[3]), .in5(in_7[3]), .in6(in_9[3]), .in7(in_10[3]),
    .out(_8bit[3]), .sel({S0, S1, S2}));  // open: in0, en
  Multiplexer #(.select(3)) multiplexer_13 (
    .in1(in_2[8]), .in2(in_3[8]), .in3(in_4[8]), .in4(in_6[8]), .in5(in_7[8]), .in6(in_9[8]), .in7(in_10[8]),
    .out(_12bit[8]), .sel({S0, S1, S2}));  // open: in0, en
  Multiplexer #(.select(3)) multiplexer_14 (
    .in1(1'b0), .in2(1'b0), .in3(in_4[15]), .in4(in_6[15]), .in5(in_7[15]), .in6(in_9[15]), .in7(in_10[15]),
    .out(_16bit[15]), .sel({S0, S1, S2}));  // open: in0, en
  Multiplexer #(.select(3)) multiplexer_15 (
    .in1(in_2[4]), .in2(in_3[4]), .in3(in_4[4]), .in4(in_6[4]), .in5(in_7[4]), .in6(in_9[4]), .in7(in_10[4]),
    .out(_8bit[4]), .sel({S0, S1, S2}));  // open: in0, en
  Multiplexer #(.select(3)) multiplexer_16 (
    .in1(in_2[9]), .in2(in_3[9]), .in3(in_4[9]), .in4(in_6[9]), .in5(in_7[9]), .in6(in_9[9]), .in7(in_10[9]),
    .out(_12bit[9]), .sel({S0, S1, S2}));  // open: in0, en

  assign _12bit[7:0] = _8bit;
  assign _16bit[11:0] = {_12bit[11:8], _8bit};

  // Other names for the same wires on the sheet: B0 = _8bit[0]; B1 = _8bit[1]; B2 = _8bit[2]; B3 = _8bit[3];
  //   B4 = _8bit[4]; B5 = _8bit[5]; B6 = _8bit[6]; B7 = _8bit[7]; B8 = _12bit[8]; B9 = _12bit[9]; B10 = _12bit[10];
  //   B11 = _12bit[11]; B12 = _16bit[12]; B13 = _16bit[13]; B14 = _16bit[14]; B15 = _16bit[15]; AR_0 = in_2[0];
  //   AR_1 = in_2[1]; AR_2 = in_2[2]; AR_3 = in_2[3]; AR_4 = in_2[4]; AR_5 = in_2[5]; AR_6 = in_2[6]; AR_7 = in_2[7];
  //   AR_8 = in_2[8]; AR_9 = in_2[9]; AR_10 = in_2[10]; AR_11 = in_2[11]; PC_0 = in_3[0]; PC_1 = in_3[1];
  //   PC_2 = in_3[2]; PC_3 = in_3[3]; PC_4 = in_3[4]; PC_5 = in_3[5]; PC_6 = in_3[6]; PC_7 = in_3[7]; PC_8 = in_3[8];
  //   PC_9 = in_3[9]; PC_10 = in_3[10]; PC_11 = in_3[11]; DR_0 = in_4[0]; DR_1 = in_4[1]; DR_2 = in_4[2];
  //   DR_3 = in_4[3]; DR_4 = in_4[4]; DR_5 = in_4[5]; DR_6 = in_4[6]; DR_7 = in_4[7]; DR_8 = in_4[8]; DR_9 = in_4[9];
  //   DR_10 = in_4[10]; DR_11 = in_4[11]; DR_12 = in_4[12]; DR_13 = in_4[13]; DR_14 = in_4[14]; DR_15 = in_4[15];
  //   AC_0 = in_6[0]; AC_1 = in_6[1]; AC_2 = in_6[2]; AC_3 = in_6[3]; AC_4 = in_6[4]; AC_5 = in_6[5]; AC_6 = in_6[6];
  //   AC_7 = in_6[7]; AC_8 = in_6[8]; AC_9 = in_6[9]; AC_10 = in_6[10]; AC_11 = in_6[11]; AC_12 = in_6[12];
  //   AC_13 = in_6[13]; AC_14 = in_6[14]; AC_15 = in_6[15]; IR_0 = in_7[0]; IR_1 = in_7[1]; IR_2 = in_7[2];
  //   IR_3 = in_7[3]; IR_4 = in_7[4]; IR_5 = in_7[5]; IR_6 = in_7[6]; IR_7 = in_7[7]; IR_8 = in_7[8]; IR_9 = in_7[9];
  //   IR_10 = in_7[10]; IR_11 = in_7[11]; IR_12 = in_7[12]; IR_13 = in_7[13]; IR_14 = in_7[14]; IR_15 = in_7[15];
  //   TR_0 = in_9[0]; TR_1 = in_9[1]; TR_2 = in_9[2]; TR_3 = in_9[3]; TR_4 = in_9[4]; TR_5 = in_9[5]; TR_6 = in_9[6];
  //   TR_7 = in_9[7]; TR_8 = in_9[8]; TR_9 = in_9[9]; TR_10 = in_9[10]; TR_11 = in_9[11]; TR_12 = in_9[12];
  //   TR_13 = in_9[13]; TR_14 = in_9[14]; TR_15 = in_9[15]; M_0 = in_10[0]; M_1 = in_10[1]; M_2 = in_10[2];
  //   M_3 = in_10[3]; M_4 = in_10[4]; M_5 = in_10[5]; M_6 = in_10[6]; M_7 = in_10[7]; M_8 = in_10[8]; M_9 = in_10[9];
  //   M_10 = in_10[10]; M_11 = in_10[11]; M_12 = in_10[12]; M_13 = in_10[13]; M_14 = in_10[14]; M_15 = in_10[15];
  //   select[2:0] = {S0, S1, S2}
endmodule

module SC (
  input  INR,
  input  CLK,
  input  CLR,
  output [3:0] \output 
);

  Counter #(.width(4), .max('hf)) counter_1 (.count(INR), .Q(\output ), .clk(CLK), .clr(CLR));  // open: load, D, carry
endmodule

module INPR (
  input  [7:0] IN,
  input  CLK,
  output [7:0] OUT
);

  Shift_Register shift_register_1 (
    .shift(1'b0), .clk(CLK), .d0(IN[7]), .q0(OUT[7]), .d1(IN[6]), .q1(OUT[6]), .d2(IN[5]), .q2(OUT[5]),
    .d3(IN[4]), .q3(OUT[4]), .d4(IN[3]), .q4(OUT[3]), .d5(IN[2]), .q5(OUT[2]), .d6(IN[1]), .q6(OUT[1]),
    .d7(IN[0]), .q7(OUT[0]));  // open: in, out, load, clr
endmodule

module OUTR (
  input  [7:0] IN,
  input  LD,
  input  CLK,
  output [7:0] OUT
);

  Shift_Register shift_register_1 (
    .shift(1'b0), .clk(CLK), .load(LD), .d0(IN[7]), .q0(OUT[7]), .d1(IN[6]), .q1(OUT[6]), .d2(IN[5]),
    .q2(OUT[5]), .d3(IN[4]), .q3(OUT[4]), .d4(IN[3]), .q4(OUT[3]), .d5(IN[2]), .q5(OUT[2]), .d6(IN[1]),
    .q6(OUT[1]), .d7(IN[0]), .q7(OUT[0]));  // open: in, out, clr
endmodule

module AC_controller (
  input  I,
  input  [15:0] T,
  input  [15:0] IR,
  input  R,
  output [6:0] LD,
  output INR,
  output CLR
);

  wire D_0, D_1, D_2, D_3, D_4, D_5, D_6, D_7, not_1_out, p, r_t;

  Decoder #(.select(3)) decoder_1 (
    .out0(D_0), .out1(D_1), .out2(D_2), .out3(D_3), .out4(D_4), .out5(D_5), .out6(D_6), .out7(D_7),
    .sel(IR[14:12]));  // open: en
  and and_1 (LD[0], D_0, T[5]);
  and and_2 (LD[1], D_1, T[5]);
  and and_3 (LD[2], D_2, T[5]);
  and and_4 (LD[3], p, IR[11]);
  and and_5 (LD[4], r_t, IR[9]);
  and and_6 (LD[5], r_t, IR[7]);
  and and_7 (LD[6], r_t, IR[6]);
  and and_8 (INR, r_t, IR[5]);
  and and_9 (CLR, r_t, IR[11]);
  not not_1 (not_1_out, I);
  and and_10 (r_t, D_7, not_1_out, T[3]);
  and and_11 (p, D_7, I, T[3]);

  // Other names for the same wires on the sheet: B_0 = IR[0]; B_1 = IR[1]; B_2 = IR[2]; B_3 = IR[3]; B_4 = IR[4];
  //   B_5 = IR[5]; B_6 = IR[6]; B_7 = IR[7]; B_8 = IR[8]; B_9 = IR[9]; B_10 = IR[10]; B_11 = IR[11]; T_0 = T[0];
  //   T_1 = T[1]; T_2 = T[2]; T_3 = T[3]; T_4 = T[4]; T_5 = T[5]; T_6 = T[6]; T_7 = T[7]; T_8 = T[8]; T_9 = T[9];
  //   T_10 = T[10]; T_11 = T[11]; T_12 = T[12]; T_13 = T[13]; T_14 = T[14]; T_15 = T[15]

  // Notes on the sheet:
  //   AND
  //   ADD
  //   DR
  //   INPR
  //   COM
  //   SHR
  //   SHL
endmodule

module PC_controller (
  input  in_1,
  input  in_2,
  input  in_3,
  input  in_4,
  input  [15:0] T,
  input  in_6,
  input  [15:0] IR,
  input  [15:0] DR,
  input  [15:0] in_9,
  output INR,
  output LD,
  output CLR
);

  wire AC_0, and_1_out, and_2_out, and_3_out, and_4_out, and_5_out, and_6_out, and_7_out, and_8_out,
       and_9_out, and_10_out, and_11_out, D_0, D_1, D_2, D_3, D_4, D_5, D_6, D_7, DR_0, not_1_out, not_2_out,
       not_3_out, not_6_out, p, r_t;
  wire [15:0] not_4_out, not_5_out;

  not not_1 (not_1_out, in_2);
  not not_2 (not_2_out, in_9[15]);
  not not_3 (not_3_out, in_3);
  and and_1 (and_1_out, not_1_out, T[1]);
  and and_2 (and_2_out, in_2, T[2]);
  and and_3 (and_3_out, D_6, T[6], DR_0);
  and and_4 (and_4_out, r_t, IR[4], not_2_out);
  and and_5 (and_5_out, r_t, IR[3], in_9[15]);
  and and_6 (and_6_out, r_t, IR[2], AC_0);
  and and_7 (and_7_out, r_t, IR[1], not_3_out);
  and and_8 (and_8_out, p, IR[9], in_4);
  and and_9 (and_9_out, p, IR[8], in_6);
  Decoder #(.select(3)) decoder_1 (
    .out0(D_0), .out1(D_1), .out2(D_2), .out3(D_3), .out4(D_4), .out5(D_5), .out6(D_6), .out7(D_7),
    .sel(IR[14:12]));  // open: en
  or or_1 (INR, and_1_out, and_2_out, and_3_out, and_4_out, and_5_out, and_6_out, and_7_out, and_8_out, and_9_out);
  and and_10 (and_10_out, D_4, T[4]);
  and and_11 (and_11_out, D_5, T[5]);
  and and_12 (CLR, in_2, T[1]);
  assign not_4_out = ~DR;  // NOT_Gate not_4, 16 bits wide
  or or_2 (LD, and_10_out, and_11_out);
  and and_13 (DR_0, not_4_out[0], not_4_out[1], not_4_out[2], not_4_out[3], not_4_out[4], not_4_out[5], not_4_out[6], not_4_out[7], not_4_out[8], not_4_out[9], not_4_out[10], not_4_out[11], not_4_out[12], not_4_out[13], not_4_out[14], not_4_out[15]);
  assign not_5_out = ~in_9;  // NOT_Gate not_5, 16 bits wide
  and and_14 (AC_0, not_5_out[0], not_5_out[1], not_5_out[2], not_5_out[3], not_5_out[4], not_5_out[5], not_5_out[6], not_5_out[7], not_5_out[8], not_5_out[9], not_5_out[10], not_5_out[11], not_5_out[12], not_5_out[13], not_5_out[14], not_5_out[15]);
  not not_6 (not_6_out, in_1);
  and and_15 (r_t, D_7, not_6_out, T[3]);
  and and_16 (p, D_7, in_1, T[3]);

  // Other names for the same wires on the sheet: E = in_3; FGI = in_4; FGO = in_6; I = in_1; AC_0_t = in_9[0];
  //   AC_1 = in_9[1]; AC_2 = in_9[2]; AC_3 = in_9[3]; AC_4 = in_9[4]; AC_5 = in_9[5]; AC_6 = in_9[6]; AC_7 = in_9[7];
  //   AC_8 = in_9[8]; AC_9 = in_9[9]; AC_10 = in_9[10]; AC_11 = in_9[11]; AC_12 = in_9[12]; AC_13 = in_9[13];
  //   AC_14 = in_9[14]; AC_15 = in_9[15]; B_0 = IR[0]; B_1 = IR[1]; B_2 = IR[2]; B_3 = IR[3]; B_4 = IR[4];
  //   B_5 = IR[5]; B_6 = IR[6]; B_7 = IR[7]; B_8 = IR[8]; B_9 = IR[9]; B_10 = IR[10]; B_11 = IR[11]; R = in_2;
  //   T_0 = T[0]; T_1 = T[1]; T_2 = T[2]; T_3 = T[3]; T_4 = T[4]; T_5 = T[5]; T_6 = T[6]; T_7 = T[7]; T_8 = T[8];
  //   T_9 = T[9]; T_10 = T[10]; T_11 = T[11]; T_12 = T[12]; T_13 = T[13]; T_14 = T[14]; T_15 = T[15]

  // Notes on the sheet:
  //   AC
endmodule

module AR_controller (
  input  I,
  input  [15:0] T,
  input  [15:0] IR,
  input  R,
  output LD,
  output INR,
  output CLR
);

  wire and_1_out, and_2_out, and_3_out, D_0, D_1, D_2, D_3, D_4, D_5, D_6, D_7, not_1_out, not_2_out;

  not not_1 (not_1_out, D_7);
  not not_2 (not_2_out, R);
  Decoder #(.select(3)) decoder_1 (
    .out0(D_0), .out1(D_1), .out2(D_2), .out3(D_3), .out4(D_4), .out5(D_5), .out6(D_6), .out7(D_7),
    .sel(IR[14:12]));  // open: en
  and and_1 (and_1_out, not_1_out, I, T[3]);
  and and_2 (and_2_out, T[2], not_2_out);
  and and_3 (and_3_out, not_2_out, T[0]);
  and and_4 (INR, D_5, T[4]);
  and and_5 (CLR, T[0], R);
  or or_1 (LD, and_1_out, and_2_out, and_3_out);

  // Other names for the same wires on the sheet: B_0 = IR[0]; B_1 = IR[1]; B_2 = IR[2]; B_3 = IR[3]; B_4 = IR[4];
  //   B_5 = IR[5]; B_6 = IR[6]; B_7 = IR[7]; B_8 = IR[8]; B_9 = IR[9]; B_10 = IR[10]; B_11 = IR[11]; T_0 = T[0];
  //   T_1 = T[1]; T_2 = T[2]; T_3 = T[3]; T_4 = T[4]; T_5 = T[5]; T_6 = T[6]; T_7 = T[7]; T_8 = T[8]; T_9 = T[9];
  //   T_10 = T[10]; T_11 = T[11]; T_12 = T[12]; T_13 = T[13]; T_14 = T[14]; T_15 = T[15]
endmodule

module DR_controller (
  input  [15:0] T,
  input  [15:0] IR,
  output LD,
  output INR
);

  wire and_1_out, and_2_out, and_3_out, and_4_out, D_0, D_1, D_2, D_3, D_4, D_5, D_6, D_7;

  Decoder #(.select(3)) decoder_1 (
    .out0(D_0), .out1(D_1), .out2(D_2), .out3(D_3), .out4(D_4), .out5(D_5), .out6(D_6), .out7(D_7),
    .sel(IR[14:12]));  // open: en
  and and_1 (and_1_out, D_0, T[4]);
  and and_2 (and_2_out, D_1, T[4]);
  and and_3 (and_3_out, D_2, T[4]);
  and and_4 (and_4_out, D_6, T[4]);
  and and_5 (INR, D_6, T[5]);
  or or_1 (LD, and_1_out, and_2_out, and_3_out, and_4_out);

  // Other names for the same wires on the sheet: B_0 = IR[0]; B_1 = IR[1]; B_2 = IR[2]; B_3 = IR[3]; B_4 = IR[4];
  //   B_5 = IR[5]; B_6 = IR[6]; B_7 = IR[7]; B_8 = IR[8]; B_9 = IR[9]; B_10 = IR[10]; B_11 = IR[11]; T_0 = T[0];
  //   T_1 = T[1]; T_2 = T[2]; T_3 = T[3]; T_4 = T[4]; T_5 = T[5]; T_6 = T[6]; T_7 = T[7]; T_8 = T[8]; T_9 = T[9];
  //   T_10 = T[10]; T_11 = T[11]; T_12 = T[12]; T_13 = T[13]; T_14 = T[14]; T_15 = T[15]
endmodule

module IR_controller (
  input  [15:0] T,
  input  in_2,
  output LD
);

  wire not_1_out;

  not not_1 (not_1_out, in_2);
  and and_1 (LD, not_1_out, T[1]);

  // Other names for the same wires on the sheet: R = in_2; T_0 = T[0]; T_1 = T[1]; T_2 = T[2]; T_3 = T[3]; T_4 = T[4];
  //   T_5 = T[5]; T_6 = T[6]; T_7 = T[7]; T_8 = T[8]; T_9 = T[9]; T_10 = T[10]; T_11 = T[11]; T_12 = T[12];
  //   T_13 = T[13]; T_14 = T[14]; T_15 = T[15]
endmodule

module TR_controller (
  input  [15:0] T,
  input  in_2,
  output LD
);

  and and_1 (LD, in_2, T[0]);

  // Other names for the same wires on the sheet: R = in_2; T_0 = T[0]; T_1 = T[1]; T_2 = T[2]; T_3 = T[3]; T_4 = T[4];
  //   T_5 = T[5]; T_6 = T[6]; T_7 = T[7]; T_8 = T[8]; T_9 = T[9]; T_10 = T[10]; T_11 = T[11]; T_12 = T[12];
  //   T_13 = T[13]; T_14 = T[14]; T_15 = T[15]
endmodule

module OUTR_controller (
  input  I,
  input  [15:0] T,
  input  [15:0] IR,
  output LD
);

  wire D_0, D_1, D_2, D_3, D_4, D_5, D_6, D_7, p;

  Decoder #(.select(3)) decoder_1 (
    .out0(D_0), .out1(D_1), .out2(D_2), .out3(D_3), .out4(D_4), .out5(D_5), .out6(D_6), .out7(D_7),
    .sel(IR[14:12]));  // open: en
  and and_1 (LD, p, IR[10]);
  and and_2 (p, D_7, I, T[3]);

  // Other names for the same wires on the sheet: B_0 = IR[0]; B_1 = IR[1]; B_2 = IR[2]; B_3 = IR[3]; B_4 = IR[4];
  //   B_5 = IR[5]; B_6 = IR[6]; B_7 = IR[7]; B_8 = IR[8]; B_9 = IR[9]; B_10 = IR[10]; B_11 = IR[11]; T_0 = T[0];
  //   T_1 = T[1]; T_2 = T[2]; T_3 = T[3]; T_4 = T[4]; T_5 = T[5]; T_6 = T[6]; T_7 = T[7]; T_8 = T[8]; T_9 = T[9];
  //   T_10 = T[10]; T_11 = T[11]; T_12 = T[12]; T_13 = T[13]; T_14 = T[14]; T_15 = T[15]
endmodule

module Memory_controller (
  input  I,
  input  [15:0] T,
  input  [15:0] IR,
  input  R,
  output READ,
  output WRITE
);

  wire and_1_out, and_2_out, and_3_out, and_4_out, and_5_out, and_6_out, and_7_out, and_8_out, and_9_out,
       and_10_out, D_0, D_1, D_2, D_3, D_4, D_5, D_6, D_7, not_1_out, not_2_out, not_3_out, p, r_t;

  Decoder #(.select(3)) decoder_1 (
    .out0(D_0), .out1(D_1), .out2(D_2), .out3(D_3), .out4(D_4), .out5(D_5), .out6(D_6), .out7(D_7),
    .sel(IR[14:12]));  // open: en
  not not_1 (not_1_out, R);
  not not_2 (not_2_out, D_7);
  and and_1 (and_1_out, not_1_out, T[1]);
  and and_2 (and_2_out, not_2_out, I, T[3]);
  and and_3 (and_3_out, D_0, T[4]);
  and and_4 (and_4_out, D_1, T[4]);
  and and_5 (and_5_out, D_2, T[4]);
  and and_6 (and_6_out, D_6, T[4]);
  and and_7 (and_7_out, R, T[1]);
  and and_8 (and_8_out, D_3, T[4]);
  and and_9 (and_9_out, D_5, T[4]);
  and and_10 (and_10_out, D_6, T[6]);
  or or_1 (READ, and_1_out, and_2_out, and_3_out, and_4_out, and_5_out, and_6_out);
  or or_2 (WRITE, and_7_out, and_8_out, and_9_out, and_10_out);
  not not_3 (not_3_out, I);
  and and_11 (r_t, D_7, not_3_out, T[3]);
  and and_12 (p, D_7, I, T[3]);

  // Other names for the same wires on the sheet: B_0 = IR[0]; B_1 = IR[1]; B_2 = IR[2]; B_3 = IR[3]; B_4 = IR[4];
  //   B_5 = IR[5]; B_6 = IR[6]; B_7 = IR[7]; B_8 = IR[8]; B_9 = IR[9]; B_10 = IR[10]; B_11 = IR[11]; T_0 = T[0];
  //   T_1 = T[1]; T_2 = T[2]; T_3 = T[3]; T_4 = T[4]; T_5 = T[5]; T_6 = T[6]; T_7 = T[7]; T_8 = T[8]; T_9 = T[9];
  //   T_10 = T[10]; T_11 = T[11]; T_12 = T[12]; T_13 = T[13]; T_14 = T[14]; T_15 = T[15]
endmodule

module SC_controller (
  input  I,
  input  [15:0] T,
  input  [15:0] IR,
  input  R,
  input  in_5,
  output CLR,
  output INR
);

  wire and_1_out, and_2_out, and_3_out, and_4_out, and_5_out, and_6_out, and_7_out, and_8_out, D_0, D_1, D_2,
       D_3, D_4, D_5, D_6, D_7, not_2_out, p, r_t;

  Decoder #(.select(3)) decoder_1 (
    .out0(D_0), .out1(D_1), .out2(D_2), .out3(D_3), .out4(D_4), .out5(D_5), .out6(D_6), .out7(D_7),
    .sel(IR[14:12]));  // open: en
  and and_1 (and_1_out, R, T[3]);
  and and_2 (and_2_out, D_0, T[6]);
  and and_3 (and_3_out, D_1, T[6]);
  and and_4 (and_4_out, D_2, T[6]);
  and and_5 (and_5_out, D_3, T[5]);
  and and_6 (and_6_out, D_4, T[5]);
  and and_7 (and_7_out, D_5, T[6]);
  and and_8 (and_8_out, D_6, T[7]);
  or or_1 (CLR, and_1_out, and_2_out, and_3_out, and_4_out, and_5_out, and_6_out, and_7_out, and_8_out, r_t, p);
  not not_1 (INR, in_5);
  not not_2 (not_2_out, I);
  and and_9 (r_t, D_7, not_2_out, T[4]);
  and and_10 (p, D_7, I, T[4]);

  // Other names for the same wires on the sheet: B_0 = IR[0]; B_1 = IR[1]; B_2 = IR[2]; B_3 = IR[3]; B_4 = IR[4];
  //   B_5 = IR[5]; B_6 = IR[6]; B_7 = IR[7]; B_8 = IR[8]; B_9 = IR[9]; B_10 = IR[10]; B_11 = IR[11]; S = in_5;
  //   T_0 = T[0]; T_1 = T[1]; T_2 = T[2]; T_3 = T[3]; T_4 = T[4]; T_5 = T[5]; T_6 = T[6]; T_7 = T[7]; T_8 = T[8];
  //   T_9 = T[9]; T_10 = T[10]; T_11 = T[11]; T_12 = T[12]; T_13 = T[13]; T_14 = T[14]; T_15 = T[15]
endmodule

module S2_S1_S0 (
  input  I,
  input  [15:0] T,
  input  [15:0] IR,
  input  R,
  output S2,
  output S1,
  output S0
);

  wire and_1_out, and_2_out, and_3_out, and_4_out, and_5_out, and_6_out, and_7_out, and_8_out, and_9_out,
       and_12_out, and_13_out, and_14_out, and_15_out, and_16_out, and_17_out, D_0, D_1, D_2, D_3, D_4, D_5,
       D_6, D_7, not_1_out, not_2_out, not_3_out, not_4_out, p, x1, x2, x3, x4, x5, x6, x7;

  and and_1 (and_1_out, D_4, T[4]);
  and and_2 (and_2_out, D_5, T[5]);
  not not_1 (not_1_out, R);
  and and_3 (and_3_out, not_1_out, T[0]);
  and and_4 (and_4_out, R, T[0]);
  and and_5 (and_5_out, D_5, T[4]);
  and and_6 (and_6_out, D_2, T[5]);
  and and_7 (and_7_out, D_6, T[6]);
  and and_8 (and_8_out, D_3, T[4]);
  and and_9 (and_9_out, p, IR[10]);
  or or_1 (x1, and_1_out, and_2_out);
  or or_2 (x2, and_3_out, and_4_out, and_5_out);
  or or_3 (x3, and_6_out, and_7_out);
  or or_4 (x4, and_8_out, and_9_out);
  Decoder #(.select(3)) decoder_1 (
    .out0(D_0), .out1(D_1), .out2(D_2), .out3(D_3), .out4(D_4), .out5(D_5), .out6(D_6), .out7(D_7),
    .sel(IR[14:12]));  // open: en
  not not_2 (not_2_out, R);
  not not_3 (not_3_out, R);
  not not_4 (not_4_out, D_7);
  and and_10 (x5, not_2_out, T[2]);
  and and_11 (x6, R, T[1]);
  and and_12 (and_12_out, not_3_out, T[1]);
  and and_13 (and_13_out, not_4_out, I, T[3]);
  and and_14 (and_14_out, D_0, T[4]);
  and and_15 (and_15_out, D_1, T[4]);
  and and_16 (and_16_out, D_2, T[4]);
  and and_17 (and_17_out, D_6, T[4]);
  or or_5 (x7, and_12_out, and_13_out, and_14_out, and_15_out, and_16_out, and_17_out);
  Priority_Encoder priority_encoder_1 (
    .in0(1'b0), .in1(x1), .in2(x2), .in3(x3), .in4(x4), .in5(x5), .in6(x6), .in7(x7), .out({S0, S1, S2}));  // open: en_in, gs, en_out
  and and_18 (p, D_7, I, T[3]);

  // Other names for the same wires on the sheet: B_0 = IR[0]; B_1 = IR[1]; B_2 = IR[2]; B_3 = IR[3]; B_4 = IR[4];
  //   B_5 = IR[5]; B_6 = IR[6]; B_7 = IR[7]; B_8 = IR[8]; B_9 = IR[9]; B_10 = IR[10]; B_11 = IR[11]; T_0 = T[0];
  //   T_1 = T[1]; T_2 = T[2]; T_3 = T[3]; T_4 = T[4]; T_5 = T[5]; T_6 = T[6]; T_7 = T[7]; T_8 = T[8]; T_9 = T[9];
  //   T_10 = T[10]; T_11 = T[11]; T_12 = T[12]; T_13 = T[13]; T_14 = T[14]; T_15 = T[15]
endmodule

module R_controller (
  input  in_1,
  input  in_2,
  input  [15:0] T,
  input  in_4,
  input  in_5,
  output J,
  output K
);

  wire not_1_out, not_2_out, not_3_out, or_1_out;

  not not_1 (not_1_out, T[0]);
  not not_2 (not_2_out, T[1]);
  not not_3 (not_3_out, T[2]);
  or or_1 (or_1_out, in_4, in_5);
  and and_1 (K, in_1, T[2]);
  and and_2 (J, not_1_out, not_2_out, not_3_out, in_2, or_1_out);

  // Other names for the same wires on the sheet: FGI = in_4; FGO = in_5; IEN = in_2; R = in_1; T_0 = T[0]; T_1 = T[1];
  //   T_2 = T[2]; T_3 = T[3]; T_4 = T[4]; T_5 = T[5]; T_6 = T[6]; T_7 = T[7]; T_8 = T[8]; T_9 = T[9]; T_10 = T[10];
  //   T_11 = T[11]; T_12 = T[12]; T_13 = T[13]; T_14 = T[14]; T_15 = T[15]
endmodule

module IEN_controller (
  input  I,
  input  [15:0] T,
  input  [15:0] IR,
  input  R,
  output J,
  output K
);

  wire and_2_out, and_3_out, D_0, D_1, D_2, D_3, D_4, D_5, D_6, D_7, p;

  Decoder #(.select(3)) decoder_1 (
    .out0(D_0), .out1(D_1), .out2(D_2), .out3(D_3), .out4(D_4), .out5(D_5), .out6(D_6), .out7(D_7),
    .sel(IR[14:12]));  // open: en
  and and_1 (J, p, IR[7]);
  and and_2 (and_2_out, p, IR[6]);
  and and_3 (and_3_out, R, T[2]);
  or or_1 (K, and_2_out, and_3_out);
  and and_4 (p, D_7, I, T[3]);

  // Other names for the same wires on the sheet: B_0 = IR[0]; B_1 = IR[1]; B_2 = IR[2]; B_3 = IR[3]; B_4 = IR[4];
  //   B_5 = IR[5]; B_6 = IR[6]; B_7 = IR[7]; B_8 = IR[8]; B_9 = IR[9]; B_10 = IR[10]; B_11 = IR[11]; T_0 = T[0];
  //   T_1 = T[1]; T_2 = T[2]; T_3 = T[3]; T_4 = T[4]; T_5 = T[5]; T_6 = T[6]; T_7 = T[7]; T_8 = T[8]; T_9 = T[9];
  //   T_10 = T[10]; T_11 = T[11]; T_12 = T[12]; T_13 = T[13]; T_14 = T[14]; T_15 = T[15]
endmodule

module E_controller (
  input  I,
  input  [15:0] T,
  input  [15:0] IR,
  input  [15:0] in_4,
  input  in_5,
  output J,
  output K
);

  wire and_1_out, and_2_out, and_3_out, and_4_out, and_5_out, and_6_out, and_7_out, and_8_out, and_9_out,
       and_10_out, and_11_out, D_0, D_1, D_2, D_3, D_4, D_5, D_6, D_7, not_1_out, not_2_out, not_3_out,
       not_4_out, r;

  Decoder #(.select(3)) decoder_1 (
    .out0(D_0), .out1(D_1), .out2(D_2), .out3(D_3), .out4(D_4), .out5(D_5), .out6(D_6), .out7(D_7),
    .sel(IR[14:12]));  // open: en
  and and_1 (and_1_out, D_1, T[5]);
  and and_2 (and_2_out, r, IR[8]);
  and and_3 (and_3_out, r, IR[7]);
  and and_4 (and_4_out, r, IR[6]);
  and and_5 (and_5_out, r, IR[10]);
  not not_1 (not_1_out, in_5);
  and and_6 (and_6_out, and_1_out, in_5);
  and and_7 (and_7_out, and_4_out, in_4[15]);
  not not_2 (not_2_out, in_4[15]);
  and and_8 (and_8_out, and_1_out, not_1_out);
  and and_9 (and_9_out, and_4_out, not_2_out);
  and and_10 (and_10_out, and_3_out, in_4[0]);
  not not_3 (not_3_out, in_4[0]);
  or or_1 (J, and_6_out, and_2_out, and_10_out, and_7_out);
  and and_11 (and_11_out, not_3_out, and_3_out);
  or or_2 (K, and_8_out, and_5_out, and_2_out, and_11_out, and_9_out);
  not not_4 (not_4_out, I);
  and and_12 (r, D_7, not_4_out, T[3]);

  // Other names for the same wires on the sheet: C_out = in_5; AC_0 = in_4[0]; AC_1 = in_4[1]; AC_2 = in_4[2];
  //   AC_3 = in_4[3]; AC_4 = in_4[4]; AC_5 = in_4[5]; AC_6 = in_4[6]; AC_7 = in_4[7]; AC_8 = in_4[8]; AC_9 = in_4[9];
  //   AC_10 = in_4[10]; AC_11 = in_4[11]; AC_12 = in_4[12]; AC_13 = in_4[13]; AC_14 = in_4[14]; AC_15 = in_4[15];
  //   B_0 = IR[0]; B_1 = IR[1]; B_2 = IR[2]; B_3 = IR[3]; B_4 = IR[4]; B_5 = IR[5]; B_6 = IR[6]; B_7 = IR[7];
  //   B_8 = IR[8]; B_9 = IR[9]; B_10 = IR[10]; B_11 = IR[11]; T_0 = T[0]; T_1 = T[1]; T_2 = T[2]; T_3 = T[3];
  //   T_4 = T[4]; T_5 = T[5]; T_6 = T[6]; T_7 = T[7]; T_8 = T[8]; T_9 = T[9]; T_10 = T[10]; T_11 = T[11];
  //   T_12 = T[12]; T_13 = T[13]; T_14 = T[14]; T_15 = T[15]

  // Notes on the sheet:
  //   AC
endmodule

module S_controller (
  input  I,
  input  [15:0] T,
  input  [15:0] IR,
  output K
);

  wire D_0, D_1, D_2, D_3, D_4, D_5, D_6, D_7, not_1_out, r;

  Decoder #(.select(3)) decoder_1 (
    .out0(D_0), .out1(D_1), .out2(D_2), .out3(D_3), .out4(D_4), .out5(D_5), .out6(D_6), .out7(D_7),
    .sel(IR[14:12]));  // open: en
  and and_1 (K, r, IR[0]);
  not not_1 (not_1_out, I);
  and and_2 (r, D_7, not_1_out, T[3]);

  // Other names for the same wires on the sheet: B_0 = IR[0]; B_1 = IR[1]; B_2 = IR[2]; B_3 = IR[3]; B_4 = IR[4];
  //   B_5 = IR[5]; B_6 = IR[6]; B_7 = IR[7]; B_8 = IR[8]; B_9 = IR[9]; B_10 = IR[10]; B_11 = IR[11]; T_0 = T[0];
  //   T_1 = T[1]; T_2 = T[2]; T_3 = T[3]; T_4 = T[4]; T_5 = T[5]; T_6 = T[6]; T_7 = T[7]; T_8 = T[8]; T_9 = T[9];
  //   T_10 = T[10]; T_11 = T[11]; T_12 = T[12]; T_13 = T[13]; T_14 = T[14]; T_15 = T[15]
endmodule

module FGI_controller (
  input  I,
  input  [15:0] T,
  input  [15:0] IR,
  input  [7:0] INPR,
  output J,
  output K
);

  wire D_0, D_1, D_2, D_3, D_4, D_5, D_6, D_7, p;

  Decoder #(.select(3)) decoder_1 (
    .out0(D_0), .out1(D_1), .out2(D_2), .out3(D_3), .out4(D_4), .out5(D_5), .out6(D_6), .out7(D_7),
    .sel(IR[14:12]));  // open: en
  or or_1 (J, INPR[0], INPR[1], INPR[2], INPR[3], INPR[4], INPR[5], INPR[6], INPR[7]);
  and and_1 (K, p, IR[11]);
  and and_2 (p, D_7, I, T[3]);

  // Other names for the same wires on the sheet: B_0 = IR[0]; B_1 = IR[1]; B_2 = IR[2]; B_3 = IR[3]; B_4 = IR[4];
  //   B_5 = IR[5]; B_6 = IR[6]; B_7 = IR[7]; B_8 = IR[8]; B_9 = IR[9]; B_10 = IR[10]; B_11 = IR[11]; T_0 = T[0];
  //   T_1 = T[1]; T_2 = T[2]; T_3 = T[3]; T_4 = T[4]; T_5 = T[5]; T_6 = T[6]; T_7 = T[7]; T_8 = T[8]; T_9 = T[9];
  //   T_10 = T[10]; T_11 = T[11]; T_12 = T[12]; T_13 = T[13]; T_14 = T[14]; T_15 = T[15]
endmodule

module FGO_controller (
  input  I,
  input  [15:0] T,
  input  [15:0] IR,
  output J,
  output K
);

  wire D_0, D_1, D_2, D_3, D_4, D_5, D_6, D_7, p;

  Decoder #(.select(3)) decoder_1 (
    .out0(D_0), .out1(D_1), .out2(D_2), .out3(D_3), .out4(D_4), .out5(D_5), .out6(D_6), .out7(D_7),
    .sel(IR[14:12]));  // open: en
  and and_1 (K, p, IR[10]);
  and and_2 (p, D_7, I, T[3]);

  assign J = T[0];

  // Other names for the same wires on the sheet: B_0 = IR[0]; B_1 = IR[1]; B_2 = IR[2]; B_3 = IR[3]; B_4 = IR[4];
  //   B_5 = IR[5]; B_6 = IR[6]; B_7 = IR[7]; B_8 = IR[8]; B_9 = IR[9]; B_10 = IR[10]; B_11 = IR[11]; T_0 = T[0];
  //   T_1 = T[1]; T_2 = T[2]; T_3 = T[3]; T_4 = T[4]; T_5 = T[5]; T_6 = T[6]; T_7 = T[7]; T_8 = T[8]; T_9 = T[9];
  //   T_10 = T[10]; T_11 = T[11]; T_12 = T[12]; T_13 = T[13]; T_14 = T[14]; T_15 = T[15]
endmodule

module I_controller (
  input  [15:0] IR,
  input  [15:0] T,
  input  R,
  output J,
  output K
);

  not not_1 (K, IR[15]);

  assign J = IR[15];

  // Other names for the same wires on the sheet: IR_15 = IR[15]; T_0 = T[0]; T_1 = T[1]; T_2 = T[2]; T_3 = T[3];
  //   T_4 = T[4]; T_5 = T[5]; T_6 = T[6]; T_7 = T[7]; T_8 = T[8]; T_9 = T[9]; T_10 = T[10]; T_11 = T[11];
  //   T_12 = T[12]; T_13 = T[13]; T_14 = T[14]; T_15 = T[15]
endmodule

module HLT (
  input  I,
  input  [15:0] T,
  input  [15:0] IR,
  output out_4
);

  wire D_0, D_1, D_2, D_3, D_4, D_5, D_6, D_7, not_1_out, r;

  Decoder #(.select(3)) decoder_1 (
    .out0(D_0), .out1(D_1), .out2(D_2), .out3(D_3), .out4(D_4), .out5(D_5), .out6(D_6), .out7(D_7),
    .sel(IR[14:12]));  // open: en
  and and_1 (out_4, r, IR[0]);
  not not_1 (not_1_out, I);
  and and_2 (r, D_7, not_1_out, T[3]);

  // Other names for the same wires on the sheet: B_0 = IR[0]; B_1 = IR[1]; B_2 = IR[2]; B_3 = IR[3]; B_4 = IR[4];
  //   B_5 = IR[5]; B_6 = IR[6]; B_7 = IR[7]; B_8 = IR[8]; B_9 = IR[9]; B_10 = IR[10]; B_11 = IR[11]; T_0 = T[0];
  //   T_1 = T[1]; T_2 = T[2]; T_3 = T[3]; T_4 = T[4]; T_5 = T[5]; T_6 = T[6]; T_7 = T[7]; T_8 = T[8]; T_9 = T[9];
  //   T_10 = T[10]; T_11 = T[11]; T_12 = T[12]; T_13 = T[13]; T_14 = T[14]; T_15 = T[15]
endmodule
